# Fritzing sketch Gloves (saved by Fritzing 0.8.7b)

parts:
  neopixel1 = Neopixel Ring 12
  FLORA1 = FLORA Color Sensor
  FLORA2 = Flora Accelerometer/Compass Sensor
  FLORA3 = Adafruit_Flora
  LED1 = Adafruit_FLORA_RGB_Smart_Pixel
  LED2 = Adafruit_FLORA_RGB_Smart_Pixel
  LED3 = Adafruit_FLORA_RGB_Smart_Pixel

nets:
  N1: neopixel1.GND, FLORA3.connector11, LED1.connector3, LED2.connector3, LED3.connector3
  N2: neopixel1.VCC, FLORA3.connector8, LED1.connector1, LED2.connector1, LED3.connector1
  N3: neopixel1.IN, FLORA3.connector13
  N4: neopixel1.OUT, LED1.connector2
  GND: FLORA1.GND, FLORA2.GND, FLORA3.connector1
  N5: FLORA1.SCL, FLORA2.SCL#6
  N6: FLORA1.SDA, FLORA2.SDA#5
  N7: FLORA1.3V, FLORA2.3V3, FLORA3.connector4
  N8: FLORA2.SCL#2, FLORA3.connector2
  N9: FLORA2.SDA#3, FLORA3.connector3
  N10: LED1.connector4, LED2.connector2
  N11: LED2.connector4, LED3.connector2

custom parts:
  Neopixel Ring 12: Neopixel Ring x12
  FLORA Color Sensor: Adafruit FLORA Color Sensor with TCS34725
  Flora Accelerometer/Compass Sensor: Flora Accelerometer and Compass Sensor - LSM303
